# Fritzing sketch Test.Gpio.HCSR04 (saved by Fritzing 0.8.3b)
breadboards: 1
perfboards: 1

parts:
  RaspberryPi1 = Raspberry Pi Model B
  HC-SR04 = IC, SIP package, 4 pins [spacing=300mil chip_label=IC]  # not connected
  R3 = Resistor [tolerance=±5% resistance=330 package=THT]
  R4 = 470 Ω Resistor [package=THT]  # not connected

nets:
  N1: RaspberryPi1.SCLK, R3.Pin_1

custom parts:
  Raspberry Pi Model B: Raspberry Pi (Model B)
